// Digital circuit ROTATER.dig as structural Verilog
module ROTATER (
  input  LI,
  input  [11:0] AI,
  input  [2:0] OP,
  output LO,
  output [11:0] AO
);

  Multiplexer #(.Selector_Bits(3)) multiplexer_1 (
    .sel(OP), .in_0(LI), .in_1(LI), .in_2(AI[11]), .in_3(AI[10]), .in_4(AI[0]), .in_5(AI[1]), .in_6(LI),
    .in_7(LI), .out(LO));
  Multiplexer #(.Selector_Bits(3)) multiplexer_2 (
    .sel(OP), .in_0(AI[0]), .in_1(AI[6]), .in_2(LI), .in_3(AI[11]), .in_4(AI[1]), .in_5(AI[2]), .in_6(AI[0]),
    .in_7(AI[0]), .out(AO[0]));
  Multiplexer #(.Selector_Bits(3)) multiplexer_3 (
    .sel(OP), .in_0(AI[1]), .in_1(AI[7]), .in_2(AI[0]), .in_3(LI), .in_4(AI[2]), .in_5(AI[3]), .in_6(AI[1]),
    .in_7(AI[1]), .out(AO[1]));
  Multiplexer #(.Selector_Bits(3)) multiplexer_4 (
    .sel(OP), .in_0(AI[2]), .in_1(AI[8]), .in_2(AI[1]), .in_3(AI[0]), .in_4(AI[3]), .in_5(AI[4]),
    .in_6(AI[2]), .in_7(AI[2]), .out(AO[2]));
  Multiplexer #(.Selector_Bits(3)) multiplexer_5 (
    .sel(OP), .in_0(AI[3]), .in_1(AI[9]), .in_2(AI[2]), .in_3(AI[1]), .in_4(AI[4]), .in_5(AI[5]),
    .in_6(AI[3]), .in_7(AI[3]), .out(AO[3]));
  Multiplexer #(.Selector_Bits(3)) multiplexer_6 (
    .sel(OP), .in_0(AI[4]), .in_1(AI[10]), .in_2(AI[3]), .in_3(AI[2]), .in_4(AI[5]), .in_5(AI[6]),
    .in_6(AI[4]), .in_7(AI[4]), .out(AO[4]));
  Multiplexer #(.Selector_Bits(3)) multiplexer_7 (
    .sel(OP), .in_0(AI[5]), .in_1(AI[11]), .in_2(AI[4]), .in_3(AI[3]), .in_4(AI[6]), .in_5(AI[7]),
    .in_6(AI[5]), .in_7(AI[5]), .out(AO[5]));
  Multiplexer #(.Selector_Bits(3)) multiplexer_8 (
    .sel(OP), .in_0(AI[6]), .in_1(AI[0]), .in_2(AI[5]), .in_3(AI[4]), .in_4(AI[7]), .in_5(AI[8]),
    .in_6(AI[6]), .in_7(AI[6]), .out(AO[6]));
  Multiplexer #(.Selector_Bits(3)) multiplexer_9 (
    .sel(OP), .in_0(AI[7]), .in_1(AI[1]), .in_2(AI[6]), .in_3(AI[5]), .in_4(AI[8]), .in_5(AI[9]),
    .in_6(AI[7]), .in_7(AI[7]), .out(AO[7]));
  Multiplexer #(.Selector_Bits(3)) multiplexer_10 (
    .sel(OP), .in_0(AI[8]), .in_1(AI[2]), .in_2(AI[7]), .in_3(AI[6]), .in_4(AI[9]), .in_5(AI[10]),
    .in_6(AI[8]), .in_7(AI[8]), .out(AO[8]));
  Multiplexer #(.Selector_Bits(3)) multiplexer_11 (
    .sel(OP), .in_0(AI[9]), .in_1(AI[3]), .in_2(AI[8]), .in_3(AI[7]), .in_4(AI[10]), .in_5(AI[11]),
    .in_6(AI[9]), .in_7(AI[9]), .out(AO[9]));
  Multiplexer #(.Selector_Bits(3)) multiplexer_12 (
    .sel(OP), .in_0(AI[10]), .in_1(AI[4]), .in_2(AI[9]), .in_3(AI[8]), .in_4(AI[11]), .in_5(LI),
    .in_6(AI[10]), .in_7(AI[10]), .out(AO[10]));
  Multiplexer #(.Selector_Bits(3)) multiplexer_13 (
    .sel(OP), .in_0(AI[11]), .in_1(AI[5]), .in_2(AI[10]), .in_3(AI[9]), .in_4(LI), .in_5(AI[0]),
    .in_6(AI[11]), .in_7(AI[11]), .out(AO[11]));

  // Notes on the sheet:
  //   LINK
  //   LSB
  //   MSB
endmodule
