// Digital circuit SEQUENCER.dig as structural Verilog
module SEQUENCER (
  input  [4:0] IN,
  output [9:0] STB_bits,
  output [9:0] CK_bits,
  output [3:0] CK_num,
  output PH_FIRST,
  output PH_STB,
  output PH_LAST
);

  wire decoder_1_out_0, decoder_1_out_2, decoder_1_out_3, decoder_1_out_4, decoder_1_out_6, decoder_1_out_7,
       decoder_1_out_9, decoder_1_out_10, decoder_1_out_12, decoder_1_out_13, decoder_1_out_15,
       decoder_1_out_16, decoder_1_out_18, decoder_1_out_19, decoder_1_out_21, decoder_1_out_22,
       decoder_1_out_24, decoder_1_out_25, decoder_1_out_27, decoder_1_out_28, decoder_1_out_30;

  Decoder #(.Selector_Bits(5)) decoder_1 (
    .sel(IN), .out_0(decoder_1_out_0), .out_1(STB_bits[0]), .out_2(decoder_1_out_2), .out_3(decoder_1_out_3),
    .out_4(decoder_1_out_4), .out_5(STB_bits[1]), .out_6(decoder_1_out_6), .out_7(decoder_1_out_7),
    .out_8(STB_bits[2]), .out_9(decoder_1_out_9), .out_10(decoder_1_out_10), .out_11(STB_bits[3]),
    .out_12(decoder_1_out_12), .out_13(decoder_1_out_13), .out_14(STB_bits[4]), .out_15(decoder_1_out_15),
    .out_16(decoder_1_out_16), .out_17(STB_bits[5]), .out_18(decoder_1_out_18), .out_19(decoder_1_out_19),
    .out_20(STB_bits[6]), .out_21(decoder_1_out_21), .out_22(decoder_1_out_22), .out_23(STB_bits[7]),
    .out_24(decoder_1_out_24), .out_25(decoder_1_out_25), .out_26(STB_bits[8]), .out_27(decoder_1_out_27),
    .out_28(decoder_1_out_28), .out_29(STB_bits[9]), .out_30(decoder_1_out_30));  // open: out_31
  or or_1 (CK_bits[0], decoder_1_out_2, STB_bits[0], decoder_1_out_0);
  or or_2 (CK_bits[1], decoder_1_out_6, STB_bits[1], decoder_1_out_4);
  or or_3 (CK_bits[2], decoder_1_out_9, STB_bits[2], decoder_1_out_7);
  or or_4 (CK_bits[3], decoder_1_out_12, STB_bits[3], decoder_1_out_10);
  or or_5 (CK_bits[4], decoder_1_out_15, STB_bits[4], decoder_1_out_13);
  or or_6 (CK_bits[5], decoder_1_out_18, STB_bits[5], decoder_1_out_16);
  or or_7 (CK_bits[6], decoder_1_out_21, STB_bits[6], decoder_1_out_19);
  or or_8 (CK_bits[7], decoder_1_out_24, STB_bits[7], decoder_1_out_22);
  or or_9 (CK_bits[8], decoder_1_out_27, STB_bits[8], decoder_1_out_25);
  or or_10 (CK_bits[9], decoder_1_out_30, STB_bits[9], decoder_1_out_28);
  or or_11 (PH_FIRST, decoder_1_out_0, decoder_1_out_4, decoder_1_out_7, decoder_1_out_10, decoder_1_out_13, decoder_1_out_16, decoder_1_out_19, decoder_1_out_22, decoder_1_out_25, decoder_1_out_28);
  or or_12 (PH_STB, STB_bits[0], STB_bits[1], STB_bits[2], STB_bits[3], STB_bits[4], STB_bits[5], STB_bits[6], STB_bits[7], STB_bits[8], STB_bits[9]);
  or or_13 (PH_LAST, decoder_1_out_2, decoder_1_out_6, decoder_1_out_9, decoder_1_out_12, decoder_1_out_15, decoder_1_out_18, decoder_1_out_21, decoder_1_out_24, decoder_1_out_27, decoder_1_out_30);
  PriorityEncoder #(.Selector_Bits(4)) priorityencoder_1 (
    .in0(CK_bits[0]), .in1(CK_bits[1]), .in2(CK_bits[2]), .in3(CK_bits[3]), .in4(CK_bits[4]),
    .in5(CK_bits[5]), .in6(CK_bits[6]), .in7(CK_bits[7]), .in8(CK_bits[8]), .in9(CK_bits[9]), .in10(1'b0),
    .in11(1'b0), .in12(1'b0), .in13(1'b0), .in14(1'b0), .in15(1'b0), .num(CK_num));  // open: any
endmodule
